// Logisim project T1_maq_fixa16x16_OK8_alunos.circ as structural Verilog: 1 circuit, main circuit main
// MaqFixa16x16
module main (
  input  S1,
  input  TOK,
  input  X1,
  input  S4,
  input  S5
);

  wire CLK, F1_out, INIT_out, multiplexer_2_out, ST;
  wire [2:0] rom_2_data;
  wire [3:0] multiplexer_1_out, register_1_q;
  wire [6:0] rom_3_data;
  wire [7:0] counter_1_q, rom_1_data;

  LED led_1 (.in(CLK));
  Clock CLOCK (.out(CLK));
  Hex_Digit_Display hex_digit_display_1 (.value(register_1_q));  // open: dp
  Register #(.width(4)) register_1 (.D(multiplexer_1_out), .Q(register_1_q), .clk(CLK), .clr(INIT_out));  // open: en
  Button INIT (.out(INIT_out));
  Hex_Digit_Display hex_digit_display_2 (.value(multiplexer_1_out));  // open: dp
  // Probe on rom_1_data
  ROM #(.addrWidth(4)) rom_1 (.addr(register_1_q), .data(rom_1_data));  // open: sel
  LED led_2 (.in(multiplexer_2_out));
  Multiplexer #(.width(4)) multiplexer_1 (
    .in0(rom_1_data[7:4]), .in1(rom_1_data[3:0]), .out(multiplexer_1_out), .sel(multiplexer_2_out));  // open: en
  Counter counter_1 (.Q(counter_1_q), .clk(CLK), .clr(ST));  // open: load, D, count, carry
  LED u_ST (.in(ST));
  LED L6 (.in(rom_3_data[6]));
  ROM #(.addrWidth(4), .dataWidth(3)) rom_2 (.addr(register_1_q), .data(rom_2_data));  // open: sel
  Multiplexer #(.select(3), .disabled(0), .enable("false")) multiplexer_2 (
    .in0(F1_out), .in1(S1), .in2(TOK), .in3(X1), .in4(S4), .in5(S5), .in6(counter_1_q[6]),
    .in7(counter_1_q[2]), .out(multiplexer_2_out), .sel(rom_2_data));
  LED L5 (.in(rom_3_data[5]));
  LED V1 (.in(rom_3_data[3]));
  LED BZ (.in(rom_3_data[4]));
  Button F1 (.out(F1_out));
  LED R1 (.in(rom_3_data[0]));
  LED LED_3 (.in(rom_3_data[1]));
  LED B1 (.in(rom_3_data[2]));
  ROM #(.addrWidth(4)) rom_3 (.addr(register_1_q), .data({ST, rom_3_data}));  // open: sel

  // Notes on the sheet:
  //    EA
  //   Máquina Fixa 16x19 com TIMER
  //   - Até 16 estados
  //   - 8x INPUTs
  //   - 8x OUTPUTs
  //   Versão de 21/02/2024
  //   SMF Lusofona LX
  //   4+4 bits
  //   ROM-ES
  //    ES
  //      ES0   |   ES1
  //   contents of rom_1 (hex, n*v repeats v):
  //   1 21 34 0 75 56 56 48 89 5a bb cc
  //   MUX - 4x2:1
  //   _ES0/ES1
  //   TIMER
  //   OUTPUTS:
  //   3 bits
  //   ROM-TST
  //   MUX - 8:1
  //   Fast
  //   Slow
  //   contents of rom_2 (hex, n*v repeats v):
  //   0 0 3 0 6 7 7 2 7 1
  //   8 bits
  //   ROM-OUT
  //   INPUTS
  //   contents of rom_3 (hex, n*v repeats v):
  //   80 80 82 82 3 0 82 3 7 87 8f 8f 90
endmodule
